# Fritzing sketch BabyPiCircuit_Board (saved by Fritzing 0.9.3b)
circuit board: 4cm x 5cm
breadboards: 1

parts:
  RPi = female pin header, 4 pins [form="♀ (female)"]
  ExtPWR = female pin header, 2 pins [form="♀ (female)"]
  100_Ohm = Resistor [tolerance=±5% resistance=100 package=THT]
  LED = female pin header, 2 pins [form="♀ (female)"]
  BC547 = NPN-Transistor [package="TO92 [THT]"]
  470_Ohm = Resistor [tolerance=±5% resistance=470 package=THT]
  DHT22 = female pin header, 4 pins [form="♀ (female)"]
  4_7_kOhm = Resistor [tolerance=±5% resistance=220 package=THT]

nets:
  N1: RPi.pin1, DHT22.pin1
  N2: RPi.pin2, 4_7_kOhm.Pin_1
  N3: RPi.pin3, 470_Ohm.Pin_0
  N4: ExtPWR.pin1, 100_Ohm.Pin_1
  N5: 100_Ohm.Pin_0, LED.pin1
  N6: LED.pin2, BC547.C
  N7: BC547.B, 470_Ohm.Pin_1
  N8: DHT22.pin2, 4_7_kOhm.Pin_0

notes:
  3V3
  GND
  PIN4
  PIN18
  PWR
  DAT
  nA
  12V
  red
  white
  Ektoras
  Savvidis
  BabyPiBoard Rev. 1
