# Fritzing sketch BabyPiCircuit_Scheme (saved by Fritzing 0.9.3b)

parts:
  R_limitLED = Resistor [tolerance=±5% resistance=100 package=THT]
  Transistor = NPN-Transistor [part_number=BC547 package="TO92 [THT]"]
  LED-Cluster = LED - 5mm [color="Infrared (940nm)" package="5 mm [THT]"]
  R_limitBase = Resistor [tolerance=±5% resistance=470 package=THT]
  PIN_18 = female pin header, 1 pin [form="♀ (female)"]
  DHT22 = female pin header, 4 pins [form="♀ (female)"]
  PIN_4 = female pin header, 1 pin [form="♀ (female)"]
  R_Data = Resistor [tolerance=±5% resistance=4.7k package=THT]

nets:
  12V: R_limitLED.Pin_0
  N1: R_limitLED.Pin_1, LED-Cluster.anode
  GND: Transistor.E, DHT22.pin4
  N2: Transistor.B, R_limitBase.Pin_1
  N3: Transistor.C, LED-Cluster.cathode
  N4: R_limitBase.Pin_0, PIN_18.pin1
  3.3V: DHT22.pin1
  N5: DHT22.pin2, R_Data.Pin_1
  N6: PIN_4.pin1, R_Data.Pin_0

notes:
  dummy
